# Fritzing sketch block schematic (saved by Fritzing 0.9.3b)

parts:
  MCU1 = Raspberry Pi Zero
  U1 = POT [package=pot_mammoth]
  SP1 = SPEAKER [package=pcb_mount_speaker]
  S1 = Pushbutton [package="[THT]"]
  Súčiastka1 = Adafruit PAM8302 [part_number="Adafruit #2130"]
  C1 = Capacitor Polarized [package=panasonic_d]
  LED1 = LED - 5mm [color="Red (633nm)" package="5 mm [THT]"]
  S3 = SWITCH-DPDT [package=mss22]
  S4 = Pushbutton [package="[THT]"]
  to_HDMI_display_brightness_switch = Header 3 [package=1x03-1mm-ra]

nets:
  N1: MCU1.pin_4, Súčiastka1.VCC
  N2: MCU1.pin_6, MCU1.pin_30, MCU1.pin_34, MCU1.pin_39, S1.Pin_1, S1.Pin_2, Súčiastka1.GND, Súčiastka1.AIN-, C1.-, LED1.cathode, S3.6, S4.Pin_1, S4.Pin_2
  N3: MCU1.pin_13, LED1.anode
  N4: MCU1.pin_29, S1.Pin_3, S1.Pin_4
  N5: MCU1.pin_31, S4.Pin_3, S4.Pin_4
  N6: MCU1.pin_33, Súčiastka1.SD
  N7: MCU1.pin_35, Súčiastka1.AIN+, C1.+
  N8: MCU1.pin_37, S3.5
  N9: U1.S, U1.E, SP1.+
  N10: U1.A, Súčiastka1.VO+
  N11: SP1.-, Súčiastka1.VO-
  N12: S3.1, to_HDMI_display_brightness_switch.2
  N13: S3.2, to_HDMI_display_brightness_switch.1

notes:
  HDMI display switch

custom parts:
  Adafruit PAM8302: This super small mono amplifier is surprisingly powerful - able to deliver up to 2.5 Watts into 4-8 ohm impedance speakers. Inside the miniature chip is a class D controller, able to run from 2.0V-5.5VDC. Since the amp is a class D, its very efficient (over 90% efficient when driving an 8Ω speaker at over half a Watt) - making it perfect for portable and battery-powered projects. It has built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
